# Fritzing sketch CIRCUIT-DIAGRAM (saved by Fritzing 0.9.3b)

parts:
  Nano = Arduino Nano (Rev3.0)
  A4988 = Pololu A4988 [package=SO16]
  MPU6050 = MPU-6050 Board GY-521 [form="♀ (female)" package=THT]
  Stepper_Motor = Stepper Motor - Bipolar
  IR = fc-51 [package=THT]
  M1 = Stepper Motor - Bipolar
  A4988_2 = Pololu A4988 [package=SO16]
  C1 = Electrolytic Capacitor [capacitance=100µF package="200 mil [THT, electrolytic]"]  # not connected
  C2 = Electrolytic Capacitor [capacitance=100µF package="200 mil [THT, electrolytic]"]  # not connected
  DC-DC_convertor_(5V_o/p) = Mini-360 DC-DC Buck converter [package=THT]
  D1 = Rectifier Diode [part_number=1N4001 package="Melf DO-213 AB [SMD]"]
  IR1 = fc-51 [package=THT]
  IR2 = fc-51 [package=THT]

nets:
  N1: Nano.D2, A4988_2.STEP
  N2: Nano.D3, A4988_2.DIR
  N3: Nano.D4, A4988.STEP
  N4: Nano.D5, A4988.DIR
  N5: Nano.D8, IR2.pin1
  N6: Nano.D9, IR.pin1
  N7: Nano.D10, IR1.pin1
  N8: Nano.VIN, DC-DC_convertor_(5V_o/p).OUT+
  N9: Nano.GND, DC-DC_convertor_(5V_o/p).OUT-
  N10: Nano.A5, MPU6050.pin3
  N11: Nano.A4, MPU6050.pin4
  N12: A4988.RESET, A4988.SLEEP
  N13: A4988.1B, Stepper_Motor.D
  N14: A4988.1A, Stepper_Motor.C
  N15: A4988.2A, Stepper_Motor.B
  N16: A4988.2B, Stepper_Motor.A
  N17: A4988.VMOT, D1.cathode
  N18: M1.A, A4988_2.2B
  N19: M1.C, A4988_2.1A
  N20: M1.B, A4988_2.2A
  N21: M1.D, A4988_2.1B
  N22: A4988_2.RESET, A4988_2.SLEEP

custom parts:
  MPU-6050 Board GY-521: Acelerometro y Giroscopio MPU-6050 Board GY-521
  Mini-360 DC-DC Buck converter: Mini-360 DC-DC Buck converter. Tiny buck step down voltage converter, input voltage 4.75 to 23V output 1 to 17V adjustable. Available from ebay and the like.
